// Logisim project control-logic.circ as structural Verilog: 1 circuit, main circuit control_logic
module control_logic (
  input  [31:0] Instruction,
  input  BrEq,
  input  BrLt,
  output PCSel,
  output RegWEn,
  output [2:0] ImmSel,
  output BrUn,
  output ASel,
  output BSel,
  output [3:0] ALUSel,
  output MemWEn,
  output [1:0] WBSel
);

  wire I_type, is_addi, is_andi, is_ori, is_slli, is_slti, is_srai, is_srli, is_xori, not_1_out, not_2_out,
       not_3_out, not_4_out, not_5_out, not_6_out, not_7_out, not_8_out, not_9_out, not_10_out, not_11_out,
       not_12_out, not_13_out, not_14_out, not_15_out, not_16_out, not_17_out, not_18_out;
  wire [5:0] address;
  wire [15:14] rom_1_data;

  not not_1 (not_1_out, Instruction[2]);
  not not_2 (not_2_out, Instruction[3]);
  and and_1 (I_type, not_1_out, not_2_out, Instruction[4], not_3_out, not_4_out);
  not not_3 (not_3_out, Instruction[5]);
  not not_4 (not_4_out, Instruction[6]);
  not not_5 (not_5_out, Instruction[12]);
  not not_6 (not_6_out, Instruction[13]);
  not not_7 (not_7_out, Instruction[14]);
  not not_8 (not_8_out, Instruction[12]);
  not not_9 (not_9_out, Instruction[12]);
  not not_10 (not_10_out, Instruction[13]);
  not not_11 (not_11_out, Instruction[30]);
  not not_12 (not_12_out, Instruction[13]);
  not not_13 (not_13_out, Instruction[14]);
  not not_14 (not_14_out, Instruction[30]);
  not not_15 (not_15_out, Instruction[13]);
  not not_16 (not_16_out, Instruction[13]);
  not not_17 (not_17_out, Instruction[12]);
  not not_18 (not_18_out, Instruction[14]);
  and and_2 (is_addi, not_5_out, not_6_out, not_7_out, I_type);
  and and_3 (is_andi, Instruction[12], Instruction[13], Instruction[14], I_type);
  and and_4 (is_ori, not_8_out, Instruction[13], Instruction[14], I_type);
  and and_5 (is_xori, not_9_out, not_10_out, Instruction[14], I_type);
  and and_6 (is_slli, Instruction[12], not_12_out, not_11_out, not_13_out, I_type);
  and and_7 (is_srli, Instruction[12], not_15_out, not_14_out, Instruction[14], I_type);
  and and_8 (is_srai, Instruction[12], not_16_out, Instruction[30], Instruction[14], I_type);
  and and_9 (is_slti, not_17_out, Instruction[13], not_18_out, I_type);
  ROM #(.addrWidth(6), .dataWidth(16)) rom_1 (
    .addr(address), .data({rom_1_data, WBSel, MemWEn, ALUSel, BSel, ASel, BrUn, ImmSel, RegWEn}));
  Priority_Encoder #(.select_enc(6)) priority_encoder_1 (
    .in0(is_addi), .in1(is_andi), .in2(is_ori), .in3(is_xori), .in4(is_slli), .in5(is_srli), .in6(is_srai),
    .in7(is_slti), .out(address));  // open: in8, in9, in10, in11, in12, in13, in14, in15, in16, in17, in18, in19, in20, in21, in22, in23, in24, in25, in26, in27, in28, in29, in30, in31, in32, in33, in34, in35, in36, in37, in38, in39, in40, in41, in42, in43, in44, in45, in46, in47, in48, in49, in50, in51, in52, in53, in54, in55, in56, in57, in58, in59, in60, in61, in62, in63, gs, en_out, en_in

  assign PCSel = 1'b0;

  // Other names for the same wires on the sheet: i2 = Instruction[2]; i3 = Instruction[3]; i4 = Instruction[4];
  //   i5 = Instruction[5]; i6 = Instruction[6]; i12 = Instruction[12]; i13 = Instruction[13]; i14 = Instruction[14];
  //   i30 = Instruction[30]

  // Notes on the sheet:
  //   INPUTS to your circuit
  //   Connect ROM Input here ->
  //   contents of rom_1 (hex, n*v repeats v):
  //   1051 13d1 1351 1251 10d1 12d1 16d1 1151
  //   ROM FOR CONTROL LOGIC
  //   DON'T CHANGE THE LOCATIONS OF THE INPUTS AND OUTPUTS!
  //   This is only if you choose to do the ROM option
  //   OUTPUT from your circuit
  //   CONNECT
  //   WIRE
  //   ROM
  //   TO
  //   USE
  //   Reminder: If using ROM, use combinational logic for PCSel
endmodule
